# Fritzing sketch AccessControlSchematic (saved by Fritzing 0.9.3b)
breadboards: 2

parts:
  Part2 = Arduino Uno (Rev3)
  S1 = Pushbutton [package="[THT]"]
  S2 = Pushbutton [package="[THT]"]
  S3 = Pushbutton [package="[THT]"]
  S4 = Pushbutton [package="[THT]"]
  S5 = Pushbutton [package="[THT]"]
  LED1 = RGB LED - (4 legs) [package="5 mm [THT]"]
  R1 = Resistor [tolerance=±5% resistance=220 package=THT]
  R2 = Resistor [tolerance=±5% resistance=220 package=THT]
  R3 = Resistor [tolerance=±5% resistance=220 package=THT]
  R4 = Resistor [tolerance=±5% resistance=220 package=THT]
  R5 = Resistor [tolerance=±5% resistance=220 package=THT]
  LCD1 = LCD screen
  LED3 = smd LED [color="Red (633nm)" package="0805 [SMD]"]
  LED4 = smd LED [color="Red (633nm)" package="0805 [SMD]"]
  U1 = POT_SWITCH [package=pot_pth_switch]

nets:
  N1: Part2.A4/SDA, S5.Pin_1, S5.Pin_2, LED3.cathode
  N2: Part2.A5/SCL, S4.Pin_3, S4.Pin_4, LED4.anode
  N3: Part2.D8, LCD1.DB3
  N4: Part2.D9_PWM, LCD1.DB4
  N5: Part2.D10_PWM/SS, LCD1.DB6
  N6: Part2.D11_PWM/MOSI, LCD1.DB7
  GND: Part2.D3_PWM, Part2.D5_PWM, Part2.D7, Part2.GND, S1.Pin_1, S1.Pin_2, S2.Pin_1, S2.Pin_2, S3.Pin_1, S3.Pin_2, LED1.common_anode, R4.Pin_0, LCD1.VSS, LCD1.R/W, LCD1.LED-, U1.G$2_2
  N7: Part2.D4, LCD1.RS
  N8: Part2.D6_PWM, LCD1.E
  5V: Part2.5V, S4.Pin_1, S4.Pin_2, S5.Pin_3, S5.Pin_4, LCD1.VDD, LCD1.LED+, U1.G$1_A
  N9: S1.Pin_3, S1.Pin_4, R1.Pin_0
  N10: S2.Pin_3, S2.Pin_4, R2.Pin_0
  N11: S3.Pin_3, S3.Pin_4, R3.Pin_0
  N12: LED1.red_cathode, R3.Pin_1
  N13: LED1.green_cathode, R2.Pin_1
  N14: LED1.blue_cathode, R1.Pin_1
  N15: R4.Pin_1, LED4.cathode
  N16: R5.Pin_1, LED3.anode
  N17: LCD1.V0, U1.G$2_1
